// Logisim project ass11.circ as structural Verilog: 7 circuits, main circuit main
module main (
);

  EightBitAdd eightbitadd_1 ();  // open: InA, InC, InB, Sum, Carry
  EightBitOr eightbitor_1 ();  // open: InA, InB, Sum
  EightBitEquality eightbitequality_1 ();  // open: InA, InB, OutA
  EightBitBarrelShifter eightbitbarrelshifter_1 ();  // open: InA, InShift, OutA
endmodule

module EightBitAdd (
  input  [7:0] InA,
  input  InC,
  input  [7:0] InB,
  output [7:0] Sum,
  output Carry
);

  wire fulladder_1_carry, fulladder_2_carry, fulladder_3_carry, fulladder_4_carry, fulladder_5_carry,
       fulladder_6_carry, fulladder_7_carry;

  FullAdder fulladder_1 (.InA(InA[0]), .InB(InB[0]), .InC(InC), .Sum(Sum[0]), .Carry(fulladder_1_carry));
  FullAdder fulladder_2 (.InA(InA[1]), .InB(InB[1]), .InC(fulladder_1_carry), .Sum(Sum[1]), .Carry(fulladder_2_carry));
  FullAdder fulladder_3 (.InA(InA[2]), .InB(InB[2]), .InC(fulladder_2_carry), .Sum(Sum[2]), .Carry(fulladder_3_carry));
  FullAdder fulladder_4 (.InA(InA[3]), .InB(InB[3]), .InC(fulladder_3_carry), .Sum(Sum[3]), .Carry(fulladder_4_carry));
  FullAdder fulladder_5 (.InA(InA[4]), .InB(InB[4]), .InC(fulladder_4_carry), .Sum(Sum[4]), .Carry(fulladder_5_carry));
  FullAdder fulladder_6 (.InA(InA[5]), .InB(InB[5]), .InC(fulladder_5_carry), .Sum(Sum[5]), .Carry(fulladder_6_carry));
  FullAdder fulladder_7 (.InA(InA[6]), .InB(InB[6]), .InC(fulladder_6_carry), .Sum(Sum[6]), .Carry(fulladder_7_carry));
  FullAdder fulladder_8 (.InA(InA[7]), .InB(InB[7]), .InC(fulladder_7_carry), .Sum(Sum[7]), .Carry(Carry));
endmodule

module FullAdder (
  input  InA,
  input  InB,
  input  InC,
  output Sum,
  output Carry
);

  wire and_1_out, and_2_out, xor_1_out;

  xor xor_1 (xor_1_out, InA, InB);
  and and_1 (and_1_out, xor_1_out, InC);
  and and_2 (and_2_out, InA, InB);
  xor xor_2 (Sum, xor_1_out, InC);
  or or_1 (Carry, and_1_out, and_2_out);
endmodule

module EightBitOr (
  input  [7:0] InA,
  input  [7:0] InB,
  output [7:0] Sum
);

  or or_1 (Sum[0], InA[0], InB[0]);
  or or_2 (Sum[1], InA[1], InB[1]);
  or or_3 (Sum[2], InA[2], InB[2]);
  or or_4 (Sum[3], InA[3], InB[3]);
  or or_5 (Sum[4], InA[4], InB[4]);
  or or_6 (Sum[5], InA[5], InB[5]);
  or or_7 (Sum[6], InA[6], InB[6]);
  or or_8 (Sum[7], InA[7], InB[7]);
endmodule

module EightBitEquality (
  input  [7:0] InA,
  input  [7:0] InB,
  output OutA
);

  wire nxor_1_outa, nxor_2_outa, nxor_3_outa, nxor_4_outa, nxor_5_outa, nxor_6_outa, nxor_7_outa, nxor_8_outa;

  NXOR nxor_1 (.InA(InA[0]), .InB(InB[0]), .OutA(nxor_1_outa));
  NXOR nxor_2 (.InA(InA[1]), .InB(InB[1]), .OutA(nxor_2_outa));
  NXOR nxor_3 (.InA(InA[2]), .InB(InB[2]), .OutA(nxor_3_outa));
  NXOR nxor_4 (.InA(InA[3]), .InB(InB[3]), .OutA(nxor_4_outa));
  NXOR nxor_5 (.InA(InA[4]), .InB(InB[4]), .OutA(nxor_5_outa));
  NXOR nxor_6 (.InA(InA[5]), .InB(InB[5]), .OutA(nxor_6_outa));
  NXOR nxor_7 (.InA(InA[6]), .InB(InB[6]), .OutA(nxor_7_outa));
  NXOR nxor_8 (.InA(InA[7]), .InB(InB[7]), .OutA(nxor_8_outa));
  and and_1 (OutA, nxor_1_outa, nxor_2_outa, nxor_3_outa, nxor_4_outa, nxor_5_outa, nxor_6_outa, nxor_7_outa, nxor_8_outa);
endmodule

module NXOR (
  input  InA,
  input  InB,
  output OutA
);

  wire xor_1_out;

  xor xor_1 (xor_1_out, InA, InB);
  not not_1 (OutA, xor_1_out);
endmodule

module EightBitBarrelShifter (
  input  [7:0] InA,
  input  [2:0] InShift,
  output [7:0] OutA
);

  wire multiplexer_1_out, multiplexer_2_out, multiplexer_3_out, multiplexer_4_out, multiplexer_5_out,
       multiplexer_6_out, multiplexer_7_out, multiplexer_8_out, multiplexer_9_out, multiplexer_10_out,
       multiplexer_11_out, multiplexer_12_out, multiplexer_13_out, multiplexer_14_out, multiplexer_15_out,
       multiplexer_16_out;

  Multiplexer multiplexer_1 (.in0(InA[7]), .in1(InA[6]), .out(multiplexer_1_out), .sel(InShift[0]));
  Multiplexer multiplexer_2 (.in0(InA[6]), .in1(InA[5]), .out(multiplexer_2_out), .sel(InShift[0]));
  Multiplexer multiplexer_3 (.in0(InA[5]), .in1(InA[4]), .out(multiplexer_3_out), .sel(InShift[0]));
  Multiplexer multiplexer_4 (.in0(InA[4]), .in1(InA[3]), .out(multiplexer_4_out), .sel(InShift[0]));
  Multiplexer multiplexer_5 (.in0(InA[3]), .in1(InA[2]), .out(multiplexer_5_out), .sel(InShift[0]));
  Multiplexer multiplexer_6 (.in0(InA[2]), .in1(InA[1]), .out(multiplexer_6_out), .sel(InShift[0]));
  Multiplexer multiplexer_7 (.in0(InA[1]), .in1(InA[0]), .out(multiplexer_7_out), .sel(InShift[0]));
  Multiplexer multiplexer_8 (.in0(InA[0]), .in1(1'b0), .out(multiplexer_8_out), .sel(InShift[0]));
  Multiplexer multiplexer_9 (
    .in0(multiplexer_1_out), .in1(multiplexer_3_out), .out(multiplexer_9_out), .sel(InShift[1]));
  Multiplexer multiplexer_10 (
    .in0(multiplexer_2_out), .in1(multiplexer_4_out), .out(multiplexer_10_out), .sel(InShift[1]));
  Multiplexer multiplexer_11 (
    .in0(multiplexer_3_out), .in1(multiplexer_5_out), .out(multiplexer_11_out), .sel(InShift[1]));
  Multiplexer multiplexer_12 (
    .in0(multiplexer_4_out), .in1(multiplexer_6_out), .out(multiplexer_12_out), .sel(InShift[1]));
  Multiplexer multiplexer_13 (
    .in0(multiplexer_5_out), .in1(multiplexer_7_out), .out(multiplexer_13_out), .sel(InShift[1]));
  Multiplexer multiplexer_14 (
    .in0(multiplexer_6_out), .in1(multiplexer_8_out), .out(multiplexer_14_out), .sel(InShift[1]));
  Multiplexer multiplexer_15 (.in0(multiplexer_7_out), .in1(1'b0), .out(multiplexer_15_out), .sel(InShift[1]));
  Multiplexer multiplexer_16 (.in0(multiplexer_8_out), .in1(1'b0), .out(multiplexer_16_out), .sel(InShift[1]));
  Multiplexer multiplexer_17 (.in0(multiplexer_9_out), .in1(multiplexer_13_out), .out(OutA[7]), .sel(InShift[2]));
  Multiplexer multiplexer_18 (.in0(multiplexer_10_out), .in1(multiplexer_14_out), .out(OutA[6]), .sel(InShift[2]));
  Multiplexer multiplexer_19 (.in0(multiplexer_11_out), .in1(multiplexer_15_out), .out(OutA[5]), .sel(InShift[2]));
  Multiplexer multiplexer_20 (.in0(multiplexer_12_out), .in1(multiplexer_16_out), .out(OutA[4]), .sel(InShift[2]));
  Multiplexer multiplexer_21 (.in0(multiplexer_13_out), .in1(1'b0), .out(OutA[3]), .sel(InShift[2]));
  Multiplexer multiplexer_22 (.in0(multiplexer_14_out), .in1(1'b0), .out(OutA[2]), .sel(InShift[2]));
  Multiplexer multiplexer_23 (.in0(multiplexer_15_out), .in1(1'b0), .out(OutA[1]), .sel(InShift[2]));
  Multiplexer multiplexer_24 (.in0(multiplexer_16_out), .in1(1'b0), .out(OutA[0]), .sel(InShift[2]));
endmodule
